// Logisim project jrmips.circ as structural Verilog: 13 circuits, main circuit Register File
module main (
);

  wire and_1_out, and_2_out, and_3_out, check_for_not_0_1_output, clock_1_out, decoder1_add, decoder1_addi,
       decoder1_addui, decoder1_and, decoder1_jr, decoder1_nor, decoder1_sll, decoder1_srl, decoder1_sub,
       decoder_2_halt, decoder_2_j, decoder_2_lw, decoder_2_put, decoder_2_sw, JALbit, multiplexer_4_out,
       multiplexer_5_out, not_1_out, not_2_out, not_3_out, or_1_out, or_2_out, or_3_out, or_4_out, or_5_out,
       or_6_out, or_7_out, output_1_if_all_0_output, priority_encoder_1_p1, priority_encoder_1_p2,
       priority_encoder_1_p4, priority_encoder_1_p5;
  wire [1:0] priority_encoder_2_out;
  wire [2:0] multiplexer_6_out;
  wire [3:0] register_1_q_2;
  wire [7:0] bit_extender_1_out, bit_extender_2_out, JAL, multiplexer_1_out, multiplexer_2_out,
       multiplexer_3_out, pc_q;
  wire [11:0] register_1_q;
  wire [15:0] ALU_output, bit_extender_3_out, demultiplexer_1_out0, demultiplexer_1_out1, extender_output,
       multiplexer_7_out, multiplexer_8_out, multiplexer_9_out, multiplexer_10_out, ram_1_data,
       reg_file_readdata1, reg_file_readdata2, rom_1_data, shift_alu_output;

  Clock clock_1 (.out(clock_1_out));
  Multiplexer #(.width(8), .enable("false")) multiplexer_1 (
    .in0(multiplexer_2_out), .in1(demultiplexer_1_out1[8:1]), .out(multiplexer_1_out), .sel(or_1_out));
  Multiplexer #(.width(8), .enable("false")) multiplexer_2 (
    .in0(multiplexer_3_out), .in1(bit_extender_1_out), .out(multiplexer_2_out), .sel(decoder1_jr));
  Register pc (.D(multiplexer_1_out), .en(1'b1), .Q(pc_q), .clk(and_1_out));  // open: clr
  and and_1 (and_1_out, clock_1_out, not_1_out);
  and and_2 (and_2_out, clock_1_out, not_1_out);
  not not_1 (not_1_out, decoder_2_halt);
  Multiplexer #(.width(8), .enable("false")) multiplexer_3 (
    .in0(JAL), .in1(demultiplexer_1_out1[8:1]), .out(multiplexer_3_out), .sel(and_3_out));
  or or_1 (or_1_out, decoder_2_j, JALbit);
  Adder adder_1 (.a(8'h1), .b(pc_q), .out(JAL), .cin(1'b0));  // open: cout
  and and_3 (and_3_out, multiplexer_4_out, or_2_out);
  ROM #(.dataWidth(16)) rom_1 (.addr(pc_q), .data(rom_1_data), .sel(1'b1));
  check_for_zero output_1_if_all_0 (.\input (reg_file_readdata1), .\output (output_1_if_all_0_output));
  Multiplexer #(.enable("false")) multiplexer_4 (
    .in0(output_1_if_all_0_output), .in1(check_for_not_0_1_output), .out(multiplexer_4_out),
    .sel(multiplexer_5_out));
  check_for_not_0 check_for_not_0_1 (.\input (reg_file_readdata1), .\output (check_for_not_0_1_output));
  Multiplexer #(.enable("false")) multiplexer_5 (
    .in0(priority_encoder_1_p1), .in1(priority_encoder_1_p2), .out(multiplexer_5_out), .sel(not_2_out));
  or or_2 (or_2_out, priority_encoder_1_p4, priority_encoder_1_p5);
  // Priority_Encoder #(.select(1), .disabled(0)) priority_encoder_1: pin names not known; wires that end beside it: priority_encoder_1_p1, priority_encoder_1_p2, or_2_out, priority_encoder_1_p4, priority_encoder_1_p5
  decoder1 decoder1 (
    .op15(rom_1_data[15]), .op14(rom_1_data[14]), .op13(rom_1_data[13]), .op12(rom_1_data[12]),
    .subop(rom_1_data[0]), .add(decoder1_add), .sub(decoder1_sub), .addi(decoder1_addi),
    .addui(decoder1_addui), .\and (decoder1_and), .\nor (decoder1_nor), .sll(decoder1_sll),
    .srl(decoder1_srl), .bx(priority_encoder_1_p5), .bz(priority_encoder_1_p4), .jr(decoder1_jr), .jal(JALbit));
  decoder2 decoder_2 (
    .op15(rom_1_data[15]), .op14(rom_1_data[14]), .op13(rom_1_data[13]), .op12(rom_1_data[12]),
    .subop(rom_1_data[0]), .j(decoder_2_j), .lw(decoder_2_lw), .sw(decoder_2_sw), .put(decoder_2_put),
    .halt(decoder_2_halt));
  not not_2 (not_2_out, or_2_out);
  or or_3 (or_3_out, decoder1_srl, decoder1_sll);
  or or_4 (or_4_out, decoder1_addi, decoder1_addui, decoder1_add);
  Demultiplexer #(.width(16), .enable("false")) demultiplexer_1 (
    .out0(demultiplexer_1_out0), .out1(demultiplexer_1_out1), .in(rom_1_data), .sel(or_5_out));
  or or_5 (or_5_out, decoder_2_j, decoder1_addi, decoder1_addui, priority_encoder_1_p5, priority_encoder_1_p4, JALbit);
  or or_6 (or_6_out, decoder_2_sw, decoder_2_lw);
  Priority_Encoder #(.select(2)) priority_encoder_2 (
    .in0(or_4_out), .in1(decoder1_sub), .in2(decoder1_and), .in3(decoder1_nor), .out(priority_encoder_2_out));  // open: gs, en_out, en_in
  or or_7 (or_7_out, decoder1_add, decoder1_sub, decoder1_addi, decoder1_addui, decoder1_and, decoder1_nor, decoder1_sll, decoder1_srl, JALbit, decoder_2_lw, decoder_2_sw);
  Multiplexer #(.width(3), .enable("false")) multiplexer_6 (
    .in0(demultiplexer_1_out0[11:9]), .in1(demultiplexer_1_out1[11:9]), .out(multiplexer_6_out),
    .sel(or_5_out));
  extender extender (.immediate(demultiplexer_1_out1[8:1]), .subop(rom_1_data[0]), .\output (extender_output));
  shift_alu shift_alu (
    .\reg (reg_file_readdata1), .subop(rom_1_data[0]), .shamt(demultiplexer_1_out0[4:1]), .enable(or_3_out),
    .\output (shift_alu_output));
  RAM #(.dataWidth(16), .bus("separate")) ram_1 (
    .addr(bit_extender_2_out), .din(reg_file_readdata1), .data(ram_1_data), .str(decoder_2_sw),
    .clk(and_2_out), .ld(decoder_2_lw));  // open: sel, clr
  Bit_Extender #(.in_width(16), .out_width(8)) bit_extender_1 (.in(reg_file_readdata1), .out(bit_extender_1_out));
  Register_File reg_file (
    .ReadRegister1(multiplexer_6_out), .ReadRegister2(demultiplexer_1_out0[8:6]),
    .WriteRegister(multiplexer_6_out), .WriteData(multiplexer_9_out), .writeEnable(or_7_out),
    .Clock(and_2_out), .ReadData1(reg_file_readdata1), .ReadData2(reg_file_readdata2));
  Multiplexer #(.width(16), .enable("false")) multiplexer_7 (
    .in0(reg_file_readdata2), .in1(extender_output), .out(multiplexer_7_out), .sel(or_5_out));
  ALU ALU (
    .first_register(reg_file_readdata1), .second_register(multiplexer_7_out),
    .instruction(priority_encoder_2_out), .\output (ALU_output));
  Bit_Extender #(.in_width(16), .out_width(8)) bit_extender_2 (.in(reg_file_readdata2), .out(bit_extender_2_out));
  Multiplexer #(.width(16), .enable("false")) multiplexer_8 (
    .in0(ALU_output), .in1(shift_alu_output), .out(multiplexer_8_out), .sel(or_3_out));
  assign bit_extender_3_out = {{8{1'b0}}, JAL};  // Bit_Extender bit_extender_3
  Multiplexer #(.width(16), .enable("false")) multiplexer_9 (
    .in0(bit_extender_3_out), .in1(multiplexer_10_out), .out(multiplexer_9_out), .sel(not_3_out));
  Multiplexer #(.width(16), .enable("false")) multiplexer_10 (
    .in0(multiplexer_8_out), .in1(ram_1_data), .out(multiplexer_10_out), .sel(or_6_out));
  not not_3 (not_3_out, JALbit);
  Hex_Digit_Display hex_digit_display_1 (.value(register_1_q_2));  // open: dp
  Hex_Digit_Display hex_digit_display_2 (.value(register_1_q[11:8]));  // open: dp
  Register #(.width(16)) register_1 (
    .D(reg_file_readdata1), .en(decoder_2_put), .Q({register_1_q_2, register_1_q}), .clk(and_2_out));  // open: clr
  Hex_Digit_Display hex_digit_display_3 (.value(register_1_q[3:0]));  // open: dp
  Hex_Digit_Display hex_digit_display_4 (.value(register_1_q[7:4]));  // open: dp
  LED led_1 (.in(decoder_2_halt));

  // Notes on the sheet:
  //   Atta Ebrahimi ate9@pitt.edu
  //   stops fecting instructions after halt
  //   contents of rom_1 (hex, n*v repeats v):
  //   1001 0 2002 1241 1200 23e0 8202 21fe 1481 2407 4008 0 25fe 8414 1001 2011 4018 1901 281f 4818 1481
  //   2409 0 16c1 1600 3700 4609 30c1 3001 4809 25fe 9442 9e2c f000
  //   jumps
  //   BRANCH
  //   temporary register to hold data to output
  //   halt intruction
endmodule

module Register_File (
  input  writeEnable,
  input  [2:0] ReadRegister1,
  input  [2:0] ReadRegister2,
  input  [2:0] WriteRegister,
  input  [15:0] WriteData,
  input  Clock,
  output [15:0] ReadData1,
  output [15:0] ReadData2
);

  wire demultiplexer_2_out0, demultiplexer_2_out1, demultiplexer_2_out2, demultiplexer_2_out3,
       demultiplexer_2_out4, demultiplexer_2_out5, demultiplexer_2_out6, demultiplexer_2_out7;
  wire [15:0] demultiplexer_1_out0, demultiplexer_1_out1, demultiplexer_1_out2, demultiplexer_1_out3,
       demultiplexer_1_out4, demultiplexer_1_out5, demultiplexer_1_out6, demultiplexer_1_out7, reg0_q,
       reg1_q, reg2_q, reg3_q, reg4_q, reg5_q, reg6_q, reg7_q;

  Demultiplexer #(.select(3), .width(16), .enable("false")) demultiplexer_1 (
    .out0(demultiplexer_1_out0), .out1(demultiplexer_1_out1), .out2(demultiplexer_1_out2),
    .out3(demultiplexer_1_out3), .out4(demultiplexer_1_out4), .out5(demultiplexer_1_out5),
    .out6(demultiplexer_1_out6), .out7(demultiplexer_1_out7), .in(WriteData), .sel(WriteRegister));
  Demultiplexer #(.select(3), .enable("false")) demultiplexer_2 (
    .out0(demultiplexer_2_out0), .out1(demultiplexer_2_out1), .out2(demultiplexer_2_out2),
    .out3(demultiplexer_2_out3), .out4(demultiplexer_2_out4), .out5(demultiplexer_2_out5),
    .out6(demultiplexer_2_out6), .out7(demultiplexer_2_out7), .in(writeEnable), .sel(WriteRegister));
  Register #(.width(16)) reg0 (
    .D(demultiplexer_1_out0), .en(demultiplexer_2_out0), .Q(reg0_q), .clk(Clock));  // open: clr
  Register #(.width(16)) reg1 (
    .D(demultiplexer_1_out1), .en(demultiplexer_2_out1), .Q(reg1_q), .clk(Clock));  // open: clr
  Register #(.width(16)) reg2 (
    .D(demultiplexer_1_out2), .en(demultiplexer_2_out2), .Q(reg2_q), .clk(Clock));  // open: clr
  Register #(.width(16)) reg3 (
    .D(demultiplexer_1_out3), .en(demultiplexer_2_out3), .Q(reg3_q), .clk(Clock));  // open: clr
  Register #(.width(16)) reg4 (
    .D(demultiplexer_1_out4), .en(demultiplexer_2_out4), .Q(reg4_q), .clk(Clock));  // open: clr
  Register #(.width(16)) reg5 (
    .D(demultiplexer_1_out5), .en(demultiplexer_2_out5), .Q(reg5_q), .clk(Clock));  // open: clr
  Register #(.width(16)) reg6 (
    .D(demultiplexer_1_out6), .en(demultiplexer_2_out6), .Q(reg6_q), .clk(Clock));  // open: clr
  Register #(.width(16)) reg7 (
    .D(demultiplexer_1_out7), .en(demultiplexer_2_out7), .Q(reg7_q), .clk(Clock));  // open: clr
  Multiplexer #(.select(3), .width(16), .enable("false")) multiplexer_1 (
    .in0(reg0_q), .in1(reg1_q), .in2(reg2_q), .in3(reg3_q), .in4(reg4_q), .in5(reg5_q), .in6(reg6_q),
    .in7(reg7_q), .out(ReadData1), .sel(ReadRegister1));
  Multiplexer #(.select(3), .width(16), .enable("false")) multiplexer_2 (
    .in0(reg0_q), .in1(reg1_q), .in2(reg2_q), .in3(reg3_q), .in4(reg4_q), .in5(reg5_q), .in6(reg6_q),
    .in7(reg7_q), .out(ReadData2), .sel(ReadRegister2));

  // Other names for the same wires on the sheet: read_register_1[2:0] = ReadRegister1;
  //   read_register_2[2:0] = ReadRegister2; write_data[15:0] = WriteData; write_register[2:0] = WriteRegister
endmodule

module ALU (
  input  [15:0] first_register,
  input  [15:0] second_register,
  input  [1:0] instruction,
  output [15:0] \output 
);

  wire [15:0] add_output, and_output, nor_output, sub_output;

  add add (.first_reg(first_register), .second_reg(second_register), .\output (add_output));
  sub sub (.first_reg(first_register), .second_reg(second_register), .\output (sub_output));
  \and  \and  (.first_reg(first_register), .second_reg(second_register), .\output (and_output));
  NOR \nor  (.first_reg(first_register), .second_reg(second_register), .\output (nor_output));
  Multiplexer #(.select(2), .width(16), .enable("false")) multiplexer_1 (
    .in0(add_output), .in1(sub_output), .in2(and_output), .in3(nor_output), .out(\output ), .sel(instruction));
endmodule

module NOR (
  input  [15:0] first_reg,
  input  [15:0] second_reg,
  output [15:0] \output 
);

  assign \output  = ~(first_reg | second_reg);  // NOR_Gate nor_1, 16 bits wide
endmodule

module sub (
  input  [15:0] first_reg,
  input  [15:0] second_reg,
  output [15:0] \output 
);

  Subtractor #(.width(16)) subtractor_1 (.a(first_reg), .b(second_reg), .out(\output ), .bin(1'b0));  // open: bout
endmodule

module add (
  input  [15:0] first_reg,
  input  [15:0] second_reg,
  output [15:0] \output 
);

  Adder #(.width(16)) adder_1 (.a(first_reg), .b(second_reg), .out(\output ), .cin(1'b0));  // open: cout
endmodule

module \and  (
  input  [15:0] first_reg,
  input  [15:0] second_reg,
  output [15:0] \output 
);

  assign \output  = first_reg & second_reg;  // AND_Gate and_1, 16 bits wide
endmodule

module decoder1 (
  input  op15,
  input  op14,
  input  op13,
  input  op12,
  input  subop,
  output add,
  output sub,
  output addi,
  output addui,
  output \and ,
  output \nor ,
  output sll,
  output srl,
  output bx,
  output bz,
  output jr,
  output jal
);

  wire not_1_out, not_2_out, not_3_out, not_4_out, not_5_out, not_6_out, not_7_out, not_8_out, not_9_out,
       not_10_out, not_11_out, not_12_out, not_13_out, not_14_out, not_15_out, not_16_out, not_17_out,
       not_18_out, not_19_out, not_20_out, not_21_out, not_22_out, not_23_out, not_24_out, not_25_out,
       not_26_out, not_27_out, not_28_out, not_29_out, not_30_out, not_31_out, not_32_out, not_33_out,
       not_34_out;

  not not_1 (not_1_out, op15);
  not not_2 (not_2_out, op14);
  not not_3 (not_3_out, op13);
  not not_4 (not_4_out, subop);
  not not_5 (not_5_out, op15);
  not not_6 (not_6_out, op14);
  not not_7 (not_7_out, op13);
  not not_8 (not_8_out, op15);
  not not_9 (not_9_out, op14);
  not not_10 (not_10_out, op12);
  not not_11 (not_11_out, subop);
  not not_12 (not_12_out, op15);
  not not_13 (not_13_out, op14);
  not not_14 (not_14_out, op12);
  not not_15 (not_15_out, op15);
  not not_16 (not_16_out, op14);
  not not_17 (not_17_out, subop);
  not not_18 (not_18_out, op15);
  not not_19 (not_19_out, op14);
  not not_20 (not_20_out, op15);
  not not_21 (not_21_out, op13);
  not not_22 (not_22_out, op12);
  not not_23 (not_23_out, subop);
  not not_24 (not_24_out, op15);
  not not_25 (not_25_out, op13);
  not not_26 (not_26_out, op12);
  not not_27 (not_27_out, op14);
  not not_28 (not_28_out, op13);
  not not_29 (not_29_out, op12);
  not not_30 (not_30_out, op14);
  not not_31 (not_31_out, op13);
  not not_32 (not_32_out, op14);
  not not_33 (not_33_out, op12);
  not not_34 (not_34_out, op14);
  and and_1 (add, not_1_out, not_2_out, not_3_out, op12, not_4_out);
  and and_2 (sub, not_5_out, not_6_out, not_7_out, op12, subop);
  and and_3 (addi, not_8_out, not_9_out, op13, not_10_out, not_11_out);
  and and_4 (addui, not_12_out, not_13_out, op13, not_14_out, subop);
  and and_5 (\and , not_15_out, not_16_out, op13, op12, not_17_out);
  and and_6 (\nor , not_18_out, not_19_out, op13, op12, subop);
  and and_7 (sll, not_20_out, op14, not_21_out, not_22_out, not_23_out);
  and and_8 (srl, not_24_out, op14, not_25_out, not_26_out, subop);
  and and_9 (bx, op15, not_27_out, not_28_out, not_29_out);
  and and_10 (bz, op15, not_30_out, not_31_out, op12);
  and and_11 (jr, op15, not_32_out, op13, not_33_out);
  and and_12 (jal, op15, not_34_out, op13, op12);
endmodule

module decoder2 (
  input  op15,
  input  op14,
  input  op13,
  input  op12,
  input  subop,
  output j,
  output lw,
  output sw,
  output put,
  output halt
);

  wire not_1_out, not_2_out, not_3_out, not_4_out, not_5_out, not_6_out, not_7_out, not_8_out, not_9_out;

  not not_1 (not_1_out, op13);
  not not_2 (not_2_out, op12);
  not not_3 (not_3_out, op15);
  not not_4 (not_4_out, subop);
  not not_5 (not_5_out, op15);
  not not_6 (not_6_out, op15);
  not not_7 (not_7_out, op14);
  not not_8 (not_8_out, op13);
  not not_9 (not_9_out, op12);
  and and_1 (j, op15, op14, not_1_out, not_2_out);
  and and_2 (lw, not_3_out, op14, op13, op12, not_4_out);
  and and_3 (sw, not_5_out, op14, op13, op12, subop);
  and and_4 (put, not_6_out, not_7_out, not_8_out, not_9_out);
  and and_5 (halt, op12, op13, op14, op15);
endmodule

module extender (
  input  [7:0] immediate,
  input  subop,
  output [15:0] \output 
);

  wire [7:0] demultiplexer_1_out0, demultiplexer_1_out1;
  wire [15:0] bit_extender_1_out, bit_extender_2_out;

  Demultiplexer #(.width(8), .enable("false")) demultiplexer_1 (
    .out0(demultiplexer_1_out0), .out1(demultiplexer_1_out1), .in(immediate), .sel(subop));
  assign bit_extender_1_out = {{8{demultiplexer_1_out0[7]}}, demultiplexer_1_out0};  // Bit_Extender bit_extender_1
  assign bit_extender_2_out = {{8{1'b0}}, demultiplexer_1_out1};  // Bit_Extender bit_extender_2
  Multiplexer #(.width(16), .enable("false")) multiplexer_1 (
    .in0(bit_extender_1_out), .in1(bit_extender_2_out), .out(\output ), .sel(subop));
endmodule

module shift_alu (
  input  [15:0] \reg ,
  input  subop,
  input  [3:0] shamt,
  input  enable,
  output [15:0] \output 
);

  wire [15:0] bit_extender_1_out, multiplexer_1_out, shifter_1_out, shifter_2_out;

  Shifter #(.width(16)) shifter_1 (.in(\reg ), .\dist (shamt), .out(shifter_1_out));
  Shifter #(.width(16), .shift("lr")) shifter_2 (.in(\reg ), .\dist (shamt), .out(shifter_2_out));
  Multiplexer #(.width(16), .enable("false")) multiplexer_1 (
    .in0(shifter_1_out), .in1(shifter_2_out), .out(multiplexer_1_out), .sel(subop));
  assign \output  = multiplexer_1_out & bit_extender_1_out;  // AND_Gate and_1, 16 bits wide
  assign bit_extender_1_out = {{15{enable}}, enable};  // Bit_Extender bit_extender_1
endmodule

module check_for_zero (
  input  [15:0] \input ,
  output \output 
);

  wire not_1_out, not_2_out, not_3_out, not_4_out, not_5_out, not_6_out, not_7_out, not_8_out, not_9_out,
       not_10_out, not_11_out, not_12_out, not_13_out, not_14_out, not_15_out, not_16_out;

  not not_1 (not_1_out, \input [0]);
  not not_2 (not_2_out, \input [1]);
  not not_3 (not_3_out, \input [2]);
  not not_4 (not_4_out, \input [3]);
  not not_5 (not_5_out, \input [4]);
  not not_6 (not_6_out, \input [5]);
  not not_7 (not_7_out, \input [6]);
  not not_8 (not_8_out, \input [7]);
  not not_9 (not_9_out, \input [8]);
  not not_10 (not_10_out, \input [9]);
  not not_11 (not_11_out, \input [10]);
  not not_12 (not_12_out, \input [11]);
  not not_13 (not_13_out, \input [12]);
  not not_14 (not_14_out, \input [13]);
  not not_15 (not_15_out, \input [14]);
  not not_16 (not_16_out, \input [15]);
  and and_1 (\output , not_1_out, not_2_out, not_3_out, not_4_out, not_5_out, not_6_out, not_7_out, not_8_out, not_10_out, not_11_out, not_12_out, not_13_out, not_14_out, not_15_out, not_16_out, not_9_out);
endmodule

module check_for_not_0 (
  input  [15:0] \input ,
  output \output 
);

  wire and_1_out, not_1_out, not_2_out, not_3_out, not_4_out, not_5_out, not_6_out, not_7_out, not_8_out,
       not_9_out, not_10_out, not_11_out, not_12_out, not_13_out, not_14_out, not_15_out, not_16_out;

  not not_1 (not_1_out, \input [0]);
  not not_2 (not_2_out, \input [1]);
  not not_3 (not_3_out, \input [2]);
  not not_4 (not_4_out, \input [3]);
  not not_5 (not_5_out, \input [4]);
  not not_6 (not_6_out, \input [5]);
  not not_7 (not_7_out, \input [6]);
  not not_8 (not_8_out, \input [7]);
  not not_9 (not_9_out, \input [8]);
  not not_10 (not_10_out, \input [9]);
  not not_11 (not_11_out, \input [10]);
  not not_12 (not_12_out, \input [11]);
  not not_13 (not_13_out, \input [12]);
  not not_14 (not_14_out, \input [13]);
  not not_15 (not_15_out, \input [14]);
  not not_16 (not_16_out, \input [15]);
  and and_1 (and_1_out, not_1_out, not_2_out, not_3_out, not_4_out, not_5_out, not_6_out, not_7_out, not_8_out, not_10_out, not_11_out, not_12_out, not_13_out, not_14_out, not_15_out, not_16_out, not_9_out);
  not not_17 (\output , and_1_out);
endmodule
